// Logisim project ICP-C01-01.circ as structural Verilog: 2 circuits, main circuit main
module main (
  input  [7:0] Store_data,
  input  [7:0] Address,
  input  clk,
  input  Store,
  input  in_5,
  input  [7:0] A,
  input  [7:0] B,
  input  [3:0] Sel,
  output [7:0] Load_store_data,
  output out_10,
  output [7:0] out_11
);

  wire alu_1_1_cout, not_1_out;

  assign Load_store_data = Store ? Store_data : 8'bz;  // Controlled_Buffer Control__Buff
  ALU_1 alu_1_1 (.Cin(in_5), .Ain(A), .Bin(B), .Cout(alu_1_1_cout), .Dout(out_11), .in_5(Sel));  // open: in_4
  not not_1 (not_1_out, Store);
  RAM ram_1 (.addr(Address), .data(Load_store_data), .clk(clk), .ld(not_1_out));  // open: sel, clr
endmodule

module ALU_1 (
  input  Cin,
  input  [7:0] Ain,
  input  [7:0] Bin,
  input  in_4,
  input  [3:0] in_5,
  output Cout,
  output [7:0] Dout
);

  wire adder_1_cout, multiplexer_1_out, subtractor_1_bout;
  wire [7:0] adder_1_out, and_1_out, negator_1_out, or_1_out, subtractor_1_out, xor_1_out;

  Adder adder_1 (.a(Ain), .b(Bin), .out(adder_1_out), .cin(Cin), .cout(adder_1_cout));
  Subtractor subtractor_1 (.a(Ain), .b(Bin), .out(subtractor_1_out), .bin(Cin), .bout(subtractor_1_bout));
  Negator negator_1 (.in(Ain), .out(negator_1_out));
  assign and_1_out = Ain & Bin;  // AND_Gate and_1, 8 bits wide
  assign or_1_out = Ain | Bin;  // OR_Gate or_1, 8 bits wide
  assign xor_1_out = Ain ^ Bin;  // XOR_Gate xor_1, 8 bits wide
  Multiplexer multiplexer_1 (
    .in0(adder_1_cout), .in1(subtractor_1_bout), .out(multiplexer_1_out), .sel(in_5[0]));  // open: en
  Multiplexer #(.select(4), .width(8)) multiplexer_2 (
    .in0(adder_1_out), .in1(subtractor_1_out), .in4(negator_1_out), .in8(and_1_out), .in9(or_1_out),
    .in10(xor_1_out), .out(Dout), .sel(in_5), .en(in_4));  // open: in2, in3, in5, in6, in7, in11, in12, in13, in14, in15
endmodule
